# Fritzing sketch BreadboardConnection (saved by Fritzing 0.9.6b)
breadboards: 1

parts:
  Част1 = Arduino Uno (Rev3)
  S1 = Momentary Switch [package=ksa_sealed_tac_switch]
  S2 = Momentary Switch [package=ksa_sealed_tac_switch]
  S3 = Momentary Switch [package=ksa_sealed_tac_switch]
  S4 = Momentary Switch [package=ksa_sealed_tac_switch]
  R5 = Resistor [tolerance=±5% resistance=1000 package="0805 [SMD]"]
  R6 = Resistor [tolerance=±5% resistance=1000 package="0805 [SMD]"]
  R7 = Resistor [tolerance=±5% resistance=1000 package="0805 [SMD]"]
  R8 = Resistor [tolerance=±5% resistance=1000 package="0805 [SMD]"]
  ZS-042_RTC1 = ZS-042 RTC Module
  U1 = LCD-16X2 [package=lcd-16x2]
  LCM1602_IIC2 = LCM1602 IIC [part_number="LCM1602 IIC" chip_label="LCM1602 IIC" package="DIP (Dual Inline) [THT]"]
  Mod1 = KY-003 Hall Magnetic Sensor Module [package="Breakout board"]  # not connected

nets:
  N1: Част1.A4/SDA, ZS-042_RTC1.SDA, LCM1602_IIC2.SDA
  N2: Част1.A5/SCL, ZS-042_RTC1.SCL, LCM1602_IIC2.SCL
  N3: Част1.D8, S3.1
  N4: Част1.D4, S1.1
  N5: Част1.D7, S2.1
  VCC: Част1.5V, R5.Pin_0, R6.Pin_0, R7.Pin_0, R8.Pin_0, ZS-042_RTC1.VCC, LCM1602_IIC2.VCC
  GND: Част1.GND, S1.4, S2.4, S3.4, S4.4, ZS-042_RTC1.GND, LCM1602_IIC2.GND
  N6: S1.2, R5.Pin_1
  N7: S2.2, R6.Pin_1
  N8: S3.2, R7.Pin_1
  N9: S4.2, R8.Pin_1
  VSS: U1.VSS, LCM1602_IIC2.VSS
  VDD: U1.VDD, LCM1602_IIC2.VDD
  N10: U1.VO, LCM1602_IIC2.V0
  N11: U1.RS, LCM1602_IIC2.RS
  N12: U1.R_W, LCM1602_IIC2.RW
  N13: U1.E, LCM1602_IIC2.E
  N14: U1.DB0, LCM1602_IIC2.D0
  N15: U1.DB1, LCM1602_IIC2.D1
  N16: U1.DB2, LCM1602_IIC2.D2
  N17: U1.DB3, LCM1602_IIC2.D3
  N18: U1.DB4, LCM1602_IIC2.D4
  N19: U1.DB5, LCM1602_IIC2.D5
  N20: U1.DB6, LCM1602_IIC2.D6
  N21: U1.DB7, LCM1602_IIC2.D7
  N22: U1.A, LCM1602_IIC2.A
  N23: U1.K, LCM1602_IIC2.K

custom parts:
  LCM1602 IIC: I2C-Module to use a 1602 or 2004 LCD on with the wire.h libory Serial LCD Modul
  KY-003 Hall Magnetic Sensor Module: KEYES KY-003 Arduino Hall Magnetic Sensor Module is a switch that will turn on/off in the presence of a magnetic field.
