# Fritzing sketch MotorController (saved by Fritzing 0.9.6b)
breadboards: 1

parts:
  R1 = Resistor [tolerance=±5% power=0.25 resistance=1000 package=THT]
  R2 = Rotary Potentiometer (Small) [maximum_resistance=100kΩ package=THT]
  D1 = Diode [package=diode-1n4001]
  Q1 = NPN-Transistor [package="TO92 [THT]"]
  M1 = DC Motor
  VCC1 = Battery block 9V

nets:
  N1: R1.Pin_0, R2.wiper
  N2: R1.Pin_1, Q1.B
  N3: R2.leg1, Q1.E, VCC1.+
  N4: R2.leg2, D1.C, M1.pin_1, VCC1.-
  N5: D1.A, Q1.C, M1.pin_2
